# Fritzing sketch conexiones dispensador (saved by Fritzing 0.9.3b)

parts:
  Componente1 = Arduino Uno (Rev3) - ICSP
  KF-1 = KF-301 Relay [package=THT]
  WATER_PUMP1 = water pump/motor
  WATER_PUMP2 = water pump/motor
  KF-2 = KF-301 Relay [package=THT]
  KF-3 = KF-301 Relay [package=THT]
  WATER_PUMP3 = water pump/motor
  LCM1602_IIC1 = LCM1602 IIC [part_number="LCM1602 IIC" chip_label="LCM1602 IIC" package="DIP (Dual Inline) [THT]"]
  LCD1 = LCD screen
  RE1 = KY-040 Rotary encoder [package=THT]

nets:
  N1: Componente1.A4/SDA, LCM1602_IIC1.SDA
  N2: Componente1.A5/SCL, LCM1602_IIC1.SCL
  N3: Componente1.D8, KF-2.signal
  N4: Componente1.D9_PWM, KF-3.signal
  N5: Componente1.D10_PWM/SS, KF-1.signal
  GND: Componente1.GND, KF-1.ground, WATER_PUMP1.pin_1, LCM1602_IIC1.GND, RE1.GND
  N6: Componente1.D2, RE1.DT
  N7: Componente1.D3_PWM, RE1.SW
  N8: Componente1.D4, RE1.CLK
  N9: Componente1.3V3, KF-1.NO
  VCC: Componente1.5V, KF-1.power, LCM1602_IIC1.VCC, RE1.Vcc
  N10: KF-1.C, WATER_PUMP1.pin_2
  N11: WATER_PUMP2.pin_2, KF-2.C
  N12: KF-3.C, WATER_PUMP3.pin_2
  VSS: LCM1602_IIC1.VSS, LCD1.VSS
  VDD: LCM1602_IIC1.VDD, LCD1.VDD
  N13: LCM1602_IIC1.V0, LCD1.V0
  N14: LCM1602_IIC1.RS, LCD1.RS
  N15: LCM1602_IIC1.RW, LCD1.R/W
  N16: LCM1602_IIC1.E, LCD1.E
  N17: LCM1602_IIC1.D0, LCD1.DB0
  N18: LCM1602_IIC1.D1, LCD1.DB1
  N19: LCM1602_IIC1.D2, LCD1.DB2
  N20: LCM1602_IIC1.D3, LCD1.DB3
  N21: LCM1602_IIC1.D4, LCD1.DB4
  N22: LCM1602_IIC1.D5, LCD1.DB5
  N23: LCM1602_IIC1.D6, LCD1.DB6
  N24: LCM1602_IIC1.D7, LCD1.DB7
  N25: LCM1602_IIC1.A, LCD1.LED+
  N26: LCM1602_IIC1.K, LCD1.LED-

custom parts:
  KF-301 Relay: KF-301
  water pump/motor: WATER PUMP BY ARDUBLOCKTR
  LCM1602 IIC: I2C-Module to use a 1602 or 2004 LCD on with the wire.h libory Serial LCD Modul
  KY-040 Rotary encoder: KY-040 Rotary Encoder with switch on breakout borad from AZ Delivery
